// Digital circuit 8bitALU.dig as structural Verilog
module _8bitALU (
  input  [7:0] A,
  input  [7:0] B,
  input  [2:0] S_1_S_0_Carry_in,
  output [7:0] D,
  output Status
);

  wire [7:0] multiplexer_1_out, not_1_out, not_2_out;

  assign not_1_out = ~B;  // Not not_1, 8 bits wide
  assign not_2_out = ~{8{1'b0}};  // Not not_2, 8 bits wide
  Multiplexer #(.Selector_Bits(2), .Bits(8)) multiplexer_1 (
    .sel(S_1_S_0_Carry_in[2:1]), .in_0(B), .in_1(not_1_out), .in_2({8{1'b0}}), .in_3(not_2_out),
    .out(multiplexer_1_out));
  _8bitAdder _8bitadder_1 (.A(A), .B(multiplexer_1_out), .Carry_in(S_1_S_0_Carry_in[0]), .Sum(D), .Carry_out(Status));

  // Notes on the sheet:
  //   D: Output
endmodule
