// Digital circuit 8bitAdder.dig as structural Verilog
module _8bitAdder (
  input  [7:0] A,
  input  [7:0] B,
  input  Carry_in,
  output [7:0] Sum,
  output Carry_out
);

  wire nathalieagalo_os_hw1_1bitadder_2_cout, nathalieagalo_os_hw1_1bitadder_3_cout,
       nathalieagalo_os_hw1_1bitadder_4_cout, nathalieagalo_os_hw1_1bitadder_5_cout,
       nathalieagalo_os_hw1_1bitadder_6_cout, nathalieagalo_os_hw1_1bitadder_7_cout,
       nathalieagalo_os_hw1_1bitadder_8_cout;

  NathalieAgalo_os_HW1_1BitAdder nathalieagalo_os_hw1_1bitadder_1 (
    .A(A[7]), .B(B[7]), .Cin(nathalieagalo_os_hw1_1bitadder_2_cout), .SUM(Sum[7]), .Cout(Carry_out));
  NathalieAgalo_os_HW1_1BitAdder nathalieagalo_os_hw1_1bitadder_2 (
    .A(A[6]), .B(B[6]), .Cin(nathalieagalo_os_hw1_1bitadder_3_cout), .SUM(Sum[6]),
    .Cout(nathalieagalo_os_hw1_1bitadder_2_cout));
  NathalieAgalo_os_HW1_1BitAdder nathalieagalo_os_hw1_1bitadder_3 (
    .A(A[5]), .B(B[5]), .Cin(nathalieagalo_os_hw1_1bitadder_4_cout), .SUM(Sum[5]),
    .Cout(nathalieagalo_os_hw1_1bitadder_3_cout));
  NathalieAgalo_os_HW1_1BitAdder nathalieagalo_os_hw1_1bitadder_4 (
    .A(A[4]), .B(B[4]), .Cin(nathalieagalo_os_hw1_1bitadder_5_cout), .SUM(Sum[4]),
    .Cout(nathalieagalo_os_hw1_1bitadder_4_cout));
  NathalieAgalo_os_HW1_1BitAdder nathalieagalo_os_hw1_1bitadder_5 (
    .A(A[3]), .B(B[3]), .Cin(nathalieagalo_os_hw1_1bitadder_6_cout), .SUM(Sum[3]),
    .Cout(nathalieagalo_os_hw1_1bitadder_5_cout));
  NathalieAgalo_os_HW1_1BitAdder nathalieagalo_os_hw1_1bitadder_6 (
    .A(A[2]), .B(B[2]), .Cin(nathalieagalo_os_hw1_1bitadder_7_cout), .SUM(Sum[2]),
    .Cout(nathalieagalo_os_hw1_1bitadder_6_cout));
  NathalieAgalo_os_HW1_1BitAdder nathalieagalo_os_hw1_1bitadder_7 (
    .A(A[1]), .B(B[1]), .Cin(nathalieagalo_os_hw1_1bitadder_8_cout), .SUM(Sum[1]),
    .Cout(nathalieagalo_os_hw1_1bitadder_7_cout));
  NathalieAgalo_os_HW1_1BitAdder nathalieagalo_os_hw1_1bitadder_8 (
    .A(A[0]), .B(B[0]), .Cin(Carry_in), .SUM(Sum[0]), .Cout(nathalieagalo_os_hw1_1bitadder_8_cout));
endmodule
