// Digital circuit 8bitCounter.dig as structural Verilog
module _8bitCounter (
  input  [7:0] Input,
  input  [1:0] Ctrl,
  input  Clk,
  output [7:0] Output
);

  wire [7:0] multiplexer_1_out;

  Multiplexer #(.Selector_Bits(2), .Bits(8)) multiplexer_1 (
    .sel(Ctrl), .in_0(Output), .in_1(Input), .in_2({8{1'b0}}), .in_3({8{1'b1}}), .out(multiplexer_1_out));
  D_FF S7 (.D(multiplexer_1_out[7]), .C(Clk), .Q(Output[7]));  // open: nQ
  D_FF S6 (.D(multiplexer_1_out[6]), .C(Clk), .Q(Output[6]));  // open: nQ
  D_FF S5 (.D(multiplexer_1_out[5]), .C(Clk), .Q(Output[5]));  // open: nQ
  D_FF S4 (.D(multiplexer_1_out[4]), .C(Clk), .Q(Output[4]));  // open: nQ
  D_FF S3 (.D(multiplexer_1_out[3]), .C(Clk), .Q(Output[3]));  // open: nQ
  D_FF S2 (.D(multiplexer_1_out[2]), .C(Clk), .Q(Output[2]));  // open: nQ
  D_FF S1 (.D(multiplexer_1_out[1]), .C(Clk), .Q(Output[1]));  // open: nQ
  D_FF S0 (.D(multiplexer_1_out[0]), .C(Clk), .Q(Output[0]));  // open: nQ

  // Notes on the sheet:
  //   00 Load
  //   01 Store
  //   10 Clear
  //   11 Set FF
endmodule
