// Digital circuit RegisterFile.dig as structural Verilog
module RegisterFile (
  input  [1:0] Read_Register_1,
  input  [1:0] Read_Register_2,
  input  [7:0] ctrl,
  input  [7:0] Write_Data,
  input  [1:0] Write_Register,
  input  clk,
  output [7:0] Read_Data_1,
  output [7:0] Read_Data_2
);

  wire [7:0] demultiplexer_1_out_0, demultiplexer_1_out_1, demultiplexer_1_out_2, demultiplexer_1_out_3,
       R0_output, R1_output, R2_output, R3_output;

  Demultiplexer #(.Bits(8), .Selector_Bits(2)) demultiplexer_1 (
    .sel(Write_Register), .in(Write_Data), .out_0(demultiplexer_1_out_0), .out_1(demultiplexer_1_out_1),
    .out_2(demultiplexer_1_out_2), .out_3(demultiplexer_1_out_3));
  _8bitCounter R0 (.Input(demultiplexer_1_out_0), .Ctrl(ctrl[1:0]), .Clk(clk), .Output(R0_output));
  _8bitCounter R1 (.Input(demultiplexer_1_out_1), .Ctrl(ctrl[3:2]), .Clk(clk), .Output(R1_output));
  _8bitCounter R2 (.Input(demultiplexer_1_out_2), .Ctrl(ctrl[5:4]), .Clk(clk), .Output(R2_output));
  _8bitCounter R3 (.Input(demultiplexer_1_out_3), .Ctrl(ctrl[7:6]), .Clk(clk), .Output(R3_output));
  Multiplexer #(.Bits(8), .Selector_Bits(2)) multiplexer_1 (
    .sel(Read_Register_1), .in_0(R0_output), .in_1(R1_output), .in_2(R2_output), .in_3(R3_output),
    .out(Read_Data_1));
  Multiplexer #(.Selector_Bits(2), .Bits(8)) multiplexer_2 (
    .sel(Read_Register_2), .in_0(R0_output), .in_1(R1_output), .in_2(R2_output), .in_3(R3_output),
    .out(Read_Data_2));
endmodule
