// Digital circuit RegisterFile_ALU.dig as structural Verilog
module RegisterFile_ALU (
  input  clk,
  input  [1:0] Read_Register1,
  input  [1:0] Read_Register2,
  input  [1:0] Write_Register,
  input  [7:0] ctrl,
  input  [2:0] Opcode,
  input  [7:0] Write_Data,
  input  Write_Select
);

  wire [7:0] _8bitalu_1_d, multiplexer_1_out, registerfile_1_read_data_1, registerfile_1_read_data_2;

  Multiplexer #(.Bits(8)) multiplexer_1 (
    .sel(Write_Select), .in_0(Write_Data), .in_1(_8bitalu_1_d), .out(multiplexer_1_out));
  RegisterFile registerfile_1 (
    .Read_Register_1(Read_Register1), .Read_Register_2(Read_Register2), .ctrl(ctrl),
    .Write_Data(multiplexer_1_out), .Write_Register(Write_Register), .clk(clk),
    .Read_Data_1(registerfile_1_read_data_1), .Read_Data_2(registerfile_1_read_data_2));
  _8bitALU _8bitalu_1 (
    .A(registerfile_1_read_data_1), .B(registerfile_1_read_data_2), .S_1_S_0_Carry_in(Opcode),
    .D(_8bitalu_1_d));  // open: Status
endmodule
